// Logisim project cpu.circ as structural Verilog: 4 circuits, main circuit main
module main (
);

  wire ALU_B_SRC, CLK, d_ff_1_q, d_ff_2_q, d_ff_3_q, d_ff_4_q, d_ff_5_q, d_ff_6_q, d_ff_7_q, MEM_ADD_OFFSET,
       MEM_READ_EN, MEM_WR_EN, not_1_out, not_2_out, not_3_out, not_4_out, undriven_4;
  wire [3:0] ALU_OP, register_1_q, undriven, undriven_2, undriven_3, undriven_5;
  wire [31:0] adder_1_out, alu_1_result, ALU_IMM, memory_1_data_out, multiplexer_1_out, multiplexer_2_out,
       multiplexer_3_out, register_2_q, register_3_q, register_4_q, register_5_q, register_6_q, register_7_q,
       register_8_q, registers_1_out_a, registers_1_out_b, registers_1_out_c;

  Clock clock_1 (.out(CLK));
  registers registers_1 (
    .DATA_IN(multiplexer_3_out), .OUT_SEL_A(undriven), .OUT_SEL_B(undriven_2), .OUT_SEL_C(undriven_3),
    .WR_EN(undriven_4), .WR_SEL(undriven_5), .OUT_A(registers_1_out_a), .OUT_B(registers_1_out_b),
    .OUT_C(registers_1_out_c));
  not not_1 (not_1_out, not_2_out);
  not not_2 (not_2_out, not_3_out);
  D_Flip_Flop d_ff_1 (.D(MEM_READ_EN), .clk(not_1_out), .Q(d_ff_1_q));  // open: Qn, preset, reset
  D_Flip_Flop d_ff_2 (.D(MEM_WR_EN), .clk(not_1_out), .Q(d_ff_2_q));  // open: Qn, preset, reset
  D_Flip_Flop d_ff_3 (.D(MEM_ADD_OFFSET), .clk(not_1_out), .Q(d_ff_3_q));  // open: Qn, preset, reset
  Register #(.width(4)) register_1 (.D(ALU_OP), .en(1'b1), .clk(not_1_out), .Q(register_1_q));  // open: clr
  D_Flip_Flop d_ff_4 (.D(ALU_B_SRC), .clk(not_1_out), .Q(d_ff_4_q));  // open: Qn, preset, reset
  Register #(.width(32)) register_2 (.D(ALU_IMM), .en(1'b1), .clk(not_1_out), .Q(register_2_q));  // open: clr
  Register #(.width(32)) register_3 (.D(registers_1_out_a), .en(not_1_out), .clk(CLK), .Q(register_3_q));  // open: clr
  Register #(.width(32)) register_4 (.D(registers_1_out_b), .en(not_1_out), .clk(CLK), .Q(register_4_q));  // open: clr
  Register #(.width(32)) register_5 (.D(registers_1_out_c), .en(not_1_out), .clk(CLK), .Q(register_5_q));  // open: clr
  Multiplexer #(.width(32)) multiplexer_1 (
    .in0(register_4_q), .in1(register_2_q), .out(multiplexer_1_out), .sel(d_ff_4_q));
  ALU alu_1 (
    .Opcode(register_1_q), .A(register_3_q), .B(multiplexer_1_out), .Result(alu_1_result));  // open: NF, ZF, CF, VF
  not not_3 (not_3_out, not_4_out);
  D_Flip_Flop d_ff_5 (.D(d_ff_1_q), .clk(not_3_out), .Q(d_ff_5_q));  // open: Qn, preset, reset
  D_Flip_Flop d_ff_6 (.D(d_ff_2_q), .clk(not_3_out), .Q(d_ff_6_q));  // open: Qn, preset, reset
  D_Flip_Flop d_ff_7 (.D(d_ff_3_q), .clk(not_3_out), .Q(d_ff_7_q));  // open: Qn, preset, reset
  Register #(.width(32)) register_6 (.D(alu_1_result), .en(not_3_out), .clk(CLK), .Q(register_6_q));  // open: clr
  Register #(.width(32)) register_7 (.D(register_4_q), .en(not_3_out), .clk(CLK), .Q(register_7_q));  // open: clr
  Register #(.width(32)) register_8 (.D(register_5_q), .en(not_3_out), .clk(CLK), .Q(register_8_q));  // open: clr
  not not_4 (not_4_out, CLK);
  Adder #(.width(32)) adder_1 (.a(register_6_q), .b(register_7_q), .out(adder_1_out));  // open: cin, cout
  Multiplexer #(.width(32)) multiplexer_2 (
    .in0(register_6_q), .in1(adder_1_out), .out(multiplexer_2_out), .sel(d_ff_7_q));
  Memory memory_1 (
    .WRITE_ENABLE(d_ff_6_q), .READ_ENABLE(d_ff_5_q), .ADDRESS_IN(multiplexer_2_out), .DATA_IN(register_8_q),
    .DATA_OUT(memory_1_data_out));
  Multiplexer #(.width(32)) multiplexer_3 (
    .in0(multiplexer_2_out), .in1(memory_1_data_out), .out(multiplexer_3_out), .sel(d_ff_5_q));
endmodule

module ALU (
  input  [3:0] Opcode,
  input  [31:0] A,
  input  [31:0] B,
  output [31:0] Result,
  output NF,
  output ZF,
  output CF,
  output VF
);

  wire [31:0] adder_1_out, and_1_out, divider_1_out, multiplier_1_out, nor_1_out, not_1_out, or_1_out,
       shifter_1_out, shifter_2_out, subtractor_1_out;

  Adder #(.width(32)) adder_1 (.a(A), .b(B), .out(adder_1_out));  // open: cin, cout
  Subtractor #(.width(32)) subtractor_1 (.a(A), .b(B), .out(subtractor_1_out));  // open: bin, bout
  Multiplier #(.width(32)) multiplier_1 (.a(A), .b(B), .out(multiplier_1_out));  // open: cin, cout
  Divider #(.width(32)) divider_1 (.a(A), .b(B), .out(divider_1_out));  // open: upper, rem
  Comparator #(.width(32)) comparator_1 (.a(A), .b(B));  // open: gt, eq, lt
  Shifter #(.width(32)) shifter_1 (.in(A), .\dist (B[4:0]), .out(shifter_1_out));
  Shifter #(.shift("lr"), .width(32)) shifter_2 (.in(A), .\dist (B[4:0]), .out(shifter_2_out));
  assign and_1_out = A & B;  // AND_Gate and_1, 32 bits wide
  assign or_1_out = A | B;  // OR_Gate or_1, 32 bits wide
  assign not_1_out = ~A;  // NOT_Gate not_1, 32 bits wide
  assign nor_1_out = ~(A | B);  // NOR_Gate nor_1, 32 bits wide
  Multiplexer #(.select(4), .width(32)) multiplexer_1 (
    .in0(adder_1_out), .in1(subtractor_1_out), .in2(multiplier_1_out), .in3(divider_1_out),
    .in5(shifter_1_out), .in6(shifter_2_out), .in7(and_1_out), .in8(or_1_out), .in9(nor_1_out),
    .in10(not_1_out), .out(Result));  // open: in4, in11, in12, in13, in14, in15, sel
  Comparator #(.width(32)) comparator_2 (.a(Result), .b({32{1'b0}}), .eq(ZF));  // open: gt, lt
endmodule

module registers (
  input  [31:0] DATA_IN,
  input  [3:0] OUT_SEL_A,
  input  [3:0] OUT_SEL_B,
  input  [3:0] OUT_SEL_C,
  input  WR_EN,
  input  [3:0] WR_SEL,
  output [31:0] OUT_A,
  output [31:0] OUT_B,
  output [31:0] OUT_C
);

  wire demultiplexer_1_out0, demultiplexer_1_out1, demultiplexer_1_out2, demultiplexer_1_out3,
       demultiplexer_1_out4, demultiplexer_1_out5, demultiplexer_1_out6, demultiplexer_1_out7,
       demultiplexer_1_out8, demultiplexer_1_out9, demultiplexer_1_out10, demultiplexer_1_out11,
       demultiplexer_1_out12, demultiplexer_1_out13, demultiplexer_1_out14, demultiplexer_1_out15;
  wire [31:0] r0_q, r1_q, r2_q, r3_q, r4_q, r5_q, r6_q, r7_q, r8_q, r9_q, r10_q, r11_q, r12_q, r14_sp_q,
       r15_bp_q, rr13_rr_q;

  Demultiplexer #(.select(4)) demultiplexer_1 (
    .out0(demultiplexer_1_out0), .out1(demultiplexer_1_out1), .out2(demultiplexer_1_out2),
    .out3(demultiplexer_1_out3), .out4(demultiplexer_1_out4), .out5(demultiplexer_1_out5),
    .out6(demultiplexer_1_out6), .out7(demultiplexer_1_out7), .out8(demultiplexer_1_out8),
    .out9(demultiplexer_1_out9), .out10(demultiplexer_1_out10), .out11(demultiplexer_1_out11),
    .out12(demultiplexer_1_out12), .out13(demultiplexer_1_out13), .out14(demultiplexer_1_out14),
    .out15(demultiplexer_1_out15), .in(WR_EN), .sel(WR_SEL));
  Register #(.width(32)) r0 (.D(DATA_IN), .en(demultiplexer_1_out0), .Q(r0_q));  // open: clk, clr
  Register #(.width(32)) r1 (.D(DATA_IN), .en(demultiplexer_1_out1), .Q(r1_q));  // open: clk, clr
  Register #(.width(32)) r2 (.D(DATA_IN), .en(demultiplexer_1_out2), .Q(r2_q));  // open: clk, clr
  Register #(.width(32)) r3 (.D(DATA_IN), .en(demultiplexer_1_out3), .Q(r3_q));  // open: clk, clr
  Register #(.width(32)) r4 (.D(DATA_IN), .en(demultiplexer_1_out4), .Q(r4_q));  // open: clk, clr
  Register #(.width(32)) r5 (.D(DATA_IN), .en(demultiplexer_1_out5), .Q(r5_q));  // open: clk, clr
  Register #(.width(32)) r6 (.D(DATA_IN), .en(demultiplexer_1_out6), .Q(r6_q));  // open: clk, clr
  Register #(.width(32)) r7 (.D(DATA_IN), .en(demultiplexer_1_out7), .Q(r7_q));  // open: clk, clr
  Register #(.width(32)) r8 (.D(DATA_IN), .en(demultiplexer_1_out8), .Q(r8_q));  // open: clk, clr
  Register #(.width(32)) r9 (.D(DATA_IN), .en(demultiplexer_1_out9), .Q(r9_q));  // open: clk, clr
  Register #(.width(32)) r10 (.D(DATA_IN), .en(demultiplexer_1_out10), .Q(r10_q));  // open: clk, clr
  Register #(.width(32)) r11 (.D(DATA_IN), .en(demultiplexer_1_out11), .Q(r11_q));  // open: clk, clr
  Register #(.width(32)) r12 (.D(DATA_IN), .en(demultiplexer_1_out12), .Q(r12_q));  // open: clk, clr
  Register #(.width(32)) rr13_rr (.D(DATA_IN), .en(demultiplexer_1_out13), .Q(rr13_rr_q));  // open: clk, clr
  Register #(.width(32)) r14_sp (.D(DATA_IN), .en(demultiplexer_1_out14), .Q(r14_sp_q));  // open: clk, clr
  Register #(.width(32)) r15_bp (.D(DATA_IN), .en(demultiplexer_1_out15), .Q(r15_bp_q));  // open: clk, clr
  Multiplexer #(.select(4), .width(32)) multiplexer_1 (
    .in0(r0_q), .in1(r1_q), .in2(r2_q), .in3(r3_q), .in4(r4_q), .in5(r5_q), .in6(r6_q), .in7(r7_q),
    .in8(r8_q), .in9(r9_q), .in10(r10_q), .in11(r11_q), .in12(r12_q), .in13(rr13_rr_q), .in14(r14_sp_q),
    .in15(r15_bp_q), .out(OUT_A), .sel(OUT_SEL_A));
  Multiplexer #(.select(4), .width(32)) multiplexer_2 (
    .in0(r0_q), .in1(r1_q), .in2(r2_q), .in3(r3_q), .in4(r4_q), .in5(r5_q), .in6(r6_q), .in7(r7_q),
    .in8(r8_q), .in9(r9_q), .in10(r10_q), .in11(r11_q), .in12(r12_q), .in13(rr13_rr_q), .in14(r14_sp_q),
    .in15(r15_bp_q), .out(OUT_B), .sel(OUT_SEL_B));
  Multiplexer #(.select(4), .width(32)) multiplexer_3 (
    .in0(r0_q), .in1(r1_q), .in2(r2_q), .in3(r3_q), .in4(r4_q), .in5(r5_q), .in6(r6_q), .in7(r7_q),
    .in8(r8_q), .in9(r9_q), .in10(r10_q), .in11(r11_q), .in12(r12_q), .in13(rr13_rr_q), .in14(r14_sp_q),
    .in15(r15_bp_q), .out(OUT_C), .sel(OUT_SEL_C));
endmodule

module Memory (
  input  WRITE_ENABLE,
  input  READ_ENABLE,
  input  [31:0] ADDRESS_IN,
  input  [31:0] DATA_IN,
  output [31:0] DATA_OUT
);
endmodule
